# Fritzing sketch sketch (saved by Fritzing 0.9.5d)
circuit board: 10.1933cm x 8.15585cm
breadboards: 1

parts:
  Composant1 = Arduino Nano (Rev3.0)
  DFRobot_DFPlayer_Mini1 = DFRobot DFPlayer Mini [part_number=DFR0299]
  Composant2 = PN532 Elechouse RFID NFC Module V3
  SP1 = SPEAKER [package=pcb_mount_speaker]
  TP1 = TP4056 [chip_label=TP4056 package="DIP (Dual Inline) [THT]"]
  U2 = LIPO-1000mAh [package=lipo-1000]
  U3 = SWITCH_SPDT [package=kps-1290]
  LED1 = smd LED [color="Green (555nm)" package="0805 [SMD]"]

nets (from the breadboard view):
  GND: Composant1.GND, DFRobot_DFPlayer_Mini1.GND-1, DFRobot_DFPlayer_Mini1.GND-2, Composant2.GND, TP1.pin6, LED1.cathode
  N1: Composant1.D6, DFRobot_DFPlayer_Mini1.TX
  N2: Composant1.D7, DFRobot_DFPlayer_Mini1.RX
  N3: Composant1.D9, LED1.anode
  N4: Composant1.VIN, U3.O
  VCC: Composant1.5V, DFRobot_DFPlayer_Mini1.VCC, Composant2.VCC
  N5: Composant1.A5, Composant2.SCL
  N6: Composant1.A4, Composant2.SDA
  N7: DFRobot_DFPlayer_Mini1.SPK_1, SP1.-
  N8: DFRobot_DFPlayer_Mini1.SPK_2, SP1.+
  N9: TP1.pin3, U3.P
  N10: TP1.pin4, U2.+
  N11: TP1.pin5, U2.-

custom parts:
  PN532 Elechouse RFID NFC Module V3: NFC is a popular technology in recent years. We often heard this work while smart phone company such as Samsung or HTC introduces their latest high-end phones. Almost all the high-end phone in the market support NFC. Near field communication (NFC) is a set of standards for smart phones and similar devices to establish radio communication with each other by touching them together or bringing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
  TP4056: A DIP stand-in part for whatever IC you want. With 6 pins on a 300mil dual inline package (DIP) footprint.

// code stored in the sketch: sketch.ino
#include <Wire.h>
#include <PN532_I2C.h>
#include <PN532.h>
#include <NfcAdapter.h>
#include <SoftwareSerial.h>
#include <DFRobotDFPlayerMini.h>

// LED
#define LED_PIN 9

// NFC reader with I2C
PN532_I2C pn532_i2c(Wire);
NfcAdapter nfc = NfcAdapter(pn532_i2c);

// MP3 Player
#define PLAYER_RX_PIN 6
#define PLAYER_TX_PIN 7
uint8_t volume = 15;
int fileCount = 0;
uint8_t fileIndex = 0;
SoftwareSerial playerSerial(PLAYER_RX_PIN, PLAYER_TX_PIN);
DFRobotDFPlayerMini player; 

void setup(void) {
  setupLed();
  setupPlayer();

  Serial.begin(115200);

  Serial.println("Initialization");
  initialize();
  Serial.println("Initialized");

  nfc.begin();
}

void setupLed() {
  pinMode(LED_PIN, OUTPUT);
}

void setupPlayer() {
  playerSerial.begin(9600);
  player.begin(playerSerial);
  player.setTimeOut(500);
  player.reset();
  player.disableDAC();
  player.volume(volume);
}

void initialize() {
  while (fileCount < 2) {
    if (player.available()) {
      fileCount = player.readFileCounts(DFPLAYER_DEVICE_SD);
    }
  }
  Serial.print("File count: ");
  Serial.println(fileCount);
}

String command = "";
void loop() {
  command = readCommandFromNFC();
  if (command != "") {
    Serial.print("Command: ");
    Serial.println(command);
  
    fileIndex = command.toInt();
    Serial.print("File index: ");
    Serial.println(fileIndex);

    blinkLed();
    player.volume(volume);
    player.playMp3Folder(fileIndex);
  }

  delay(500);
}

void blinkLed() {
  digitalWrite(LED_PIN, HIGH);
  delay(500);
  digitalWrite(LED_PIN, LOW); 
}

String readCommandFromNFC() {
  if (!nfc.tagPresent()) {
    return "";
  }
  
  NfcTag tag = nfc.read();

  if (!tag.hasNdefMessage()) {
    return "";
  }

  
  NdefMessage message = tag.getNdefMessage();
  int recordCount = message.getRecordCount();
  for (int i = 0; i < recordCount; i++) {
    NdefRecord record = message.getRecord(i);

    /*
    Serial.print("  TNF: ");
    Serial.println(record.getTnf());
    Serial.print("  Type: ");
    Serial.println(record.getType()); // will be "" for TNF_EMPTY
    */

    // The TNF and Type should be used to determine how your application processes the payload
    // There's no generic processing for the payload, it's returned as a byte[]
    int payloadLength = record.getPayloadLength();
    byte payload[payloadLength];
    record.getPayload(payload);
    //Serial.print("  Payload (HEX): ");
    //PrintHexChar(payload, payloadLength);

    // Skip characters because the payload contains headers
    int skipCharacterCount = (int) payload[0] + 1;
    String payloadAsString = "";
    for (int characterIndex = skipCharacterCount; characterIndex < payloadLength; characterIndex++) {
      payloadAsString += (char)payload[characterIndex];
    }
    //Serial.print("  Payload (as String): ");
    //Serial.println(payloadAsString);
    return payloadAsString;
  }
}
